# Fritzing sketch parking-sensor (saved by Fritzing 0.9.3b)
breadboards: 1

parts:
  Raspberry_Pi_1 = Raspberry Pi 3 [part_number=RPI-3-V1.2]
  hc-sr1 = hc-sr04
  부품1 = Passive Buzzer
  LED1 = smd LED [color="Blue (525nm)" package="0805 [SMD]"]
  LED2 = smd LED [color="Yellow (595nm)" package="0805 [SMD]"]
  LED3 = smd LED [color="Red (633nm)" package="0805 [SMD]"]
  R3 = Resistor [tolerance=±5% resistance=220 package=THT]
  R4 = Resistor [tolerance=±5% resistance=220 package=THT]
  R5 = Resistor [tolerance=±5% resistance=220 package=THT]

nets:
  N1: Raspberry_Pi_1.3v3, 부품1.S
  GND: Raspberry_Pi_1.GND, hc-sr1.GND, 부품1.GND, R3.Pin_1, R4.Pin_1, R5.Pin_1
  N2: Raspberry_Pi_1.GPIO17, LED3.anode
  N3: Raspberry_Pi_1.GPIO27, LED2.anode
  N4: Raspberry_Pi_1.GPIO22, LED1.anode
  N5: Raspberry_Pi_1.GPIO18, 부품1.NC
  N6: Raspberry_Pi_1.GPIO15, hc-sr1.Trig
  N7: Raspberry_Pi_1.GPIO14, hc-sr1.Echo
  5V: Raspberry_Pi_1.5V, hc-sr1.VCC
  N8: LED1.cathode, R3.Pin_0
  N9: LED2.cathode, R4.Pin_0
  N10: LED3.cathode, R5.Pin_0
